# Fritzing sketch current_sensor (saved by Fritzing 0.9.3b)
breadboards: 1

parts:
  パーツ1 = INA219 High Side DC Current Sensor Breakout [part_number=904]
  パーツ2 = Adafruit Pro Trinket 3.3V 12MHz [part_number="Adafruit #2010"]
  パーツ3 = Bluetooth HC-05 Macho  # not connected
  パーツ4 = Adafruit Switched JST Breakout [part_number="Adafruit #1863"]
  U1 = LIPO-110mAh [package=lipo-110]  # not connected
  M1 = DC Motor
  BAT2 = Battery Holders [package=battery-aa-kit]
  BAT3 = Battery Holders [package=battery-aa-kit]

nets:
  N1: パーツ1.VIN-, M1.pin_1
  N2: パーツ1.VIN+, BAT3.+
  N3: パーツ2.VBAT, パーツ4.SW, M1.pin_2, BAT2.-
  GND: パーツ2.GND, パーツ4.GND
  N4: BAT2.+, BAT3.-

notes:
  ミニ四駆
  BTモジュール
  INA219 High Side DC Current Sensor Breakout
  PRO TRINKET 3V
  Li-Poバッテリーコネクタ

custom parts:
  INA219 High Side DC Current Sensor Breakout: This breakout board will solve all your power-monitoring problems. Instead of struggling with two multimeters, you can just use the handy INA219B chip on this breakout to both measure both the high side voltage and DC current draw over I2C with 1% precision. Most current-measuring devices such as our current panel meter are only good for low side measuring. That means that unless you want to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
  Adafruit Pro Trinket 3.3V 12MHz: rinket's got a big sister in town - the Pro Trinket 3V! Pro Trinket combines everything you love about Trinket with the familiarity of the core Arduino chip, the ATmega328. It's like an Arduino Pro Mini with more pins and USB tossed in. Trinket's a year old now, and while its been great to see tons of tiny projects, sometimes you just need more pins, more FLASH, and more RAM. That's why we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
  Adafruit Switched JST Breakout: This switched JST connector is the best way to quickly prototype with our LiPoly batteries. We paired a genuine JST connector with a slide switch that can do up to 600mA. Both are soldered onto a breadboard-friendly breakout. There's two ground pins, one 'switched' power pin, and one pin that is always on. This is compatible with the "JST PH 2-pin" connectors we use in our battery packs..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
