# Fritzing sketch current_sensor2 (saved by Fritzing 0.9.3b)
breadboards: 1

parts:
  パーツ2 = Adafruit Pro Trinket 3.3V 12MHz [part_number="Adafruit #2010"]
  M1 = DC Motor
  BAT2 = Battery Holders [package=battery-aa-kit]
  BAT3 = Battery Holders [package=battery-aa-kit]
  パーツ3 = Bluetooth HC-05 Macho  # not connected
  BAT4 = Battery Holders [package=battcon_12mm]

nets:
  N1: パーツ2.GND, BAT4.-
  N2: パーツ2.+3V3, BAT4.+
  N3: M1.pin_2, BAT2.-
  N4: BAT2.+, BAT3.-

notes:
  ミニ四駆
  BTモジュール
  INA260 DC Current Sensor
  PRO TRINKET 3V

custom parts:
  Adafruit Pro Trinket 3.3V 12MHz: rinket's got a big sister in town - the Pro Trinket 3V! Pro Trinket combines everything you love about Trinket with the familiarity of the core Arduino chip, the ATmega328. It's like an Arduino Pro Mini with more pins and USB tossed in. Trinket's a year old now, and while its been great to see tons of tiny projects, sometimes you just need more pins, more FLASH, and more RAM. That's why we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
